# Fritzing sketch diagram (saved by Fritzing 0.9.3b)
breadboards: 1

parts:
  S1 = Pushbutton [package="[THT]"]
  S2 = Pushbutton [package="[THT]"]
  S3 = Pushbutton [package="[THT]"]
  S4 = Pushbutton [package="[THT]"]
  Part1 = Arduino Leonardo (Rev3b)
  DHT1 = DHT11_Temperature_and_Humitidy_Sensor
  ZS-042_RTC1 = ZS-042 RTC Module
  OLED1 = OLED 128x64 I2C Monochrome Display

nets:
  N1: S1.Pin_1, S1.Pin_2, Part1.D2/SDA, Part1.SDA, ZS-042_RTC1.SDA, OLED1.connector8
  GND: S1.Pin_3, S1.Pin_4, S2.Pin_3, S2.Pin_4, S3.Pin_3, S3.Pin_4, S4.Pin_3, S4.Pin_4, Part1.GND, DHT1.connector4, ZS-042_RTC1.GND, OLED1.connector4
  N2: S2.Pin_1, S2.Pin_2, Part1.D3_PWM/SCL, Part1.SCL, ZS-042_RTC1.SCL, OLED1.connector7
  N3: S3.Pin_1, S3.Pin_2, Part1.D4/A6
  N4: S4.Pin_1, S4.Pin_2, Part1.D5_PWM
  3V3: Part1.3V3, DHT1.connector3, ZS-042_RTC1.VCC, OLED1.connector5
  N5: Part1.D12/A11, DHT1.connector2
